# Fritzing sketch stereotaxic wiring v-combine with board picture (saved by Fritzing 1.0.4)

parts:
  J1 = Power Jack [package=power_jack_smd]
  U4 = SWITCH_SPDT [package=kps-1290]  # not connected
  Raspberry_Pi_2 = Raspberry Pi 3 [part_number=RPI-3-V1.2]  # not connected
  U5 = ENCODER-QUADRATURE [package=encoder-16mm-quad]  # not connected
  M1 = Stepper Motor - Bipolar  # not connected
  M2 = Stepper Motor - Bipolar  # not connected
  M3 = Stepper Motor - Bipolar  # not connected
  S24 = Toggle Switch [package=THT]  # not connected
  S25 = Toggle Switch [package=THT]  # not connected
  S26 = Toggle Switch [package=THT]  # not connected
  M4 = RioRand LM2596
  S27 = Taiway 100-SP-X-T1 SPDT Miniature Toggle Switch [part_number=100-SP-X-T1-0-0-B1-M2 package=THT]
  U8 = Graphical LCD 128x64 [package=lcd-g12864]
  S31 = Pushbutton [package="[SMD]"]  # not connected
  S32 = Pushbutton [package="[SMD]"]  # not connected
  S33 = Pushbutton [package="[SMD]"]  # not connected
  S34 = Pushbutton [package="[SMD]"]  # not connected
  S35 = Pushbutton [package="[SMD]"]  # not connected
  S36 = Pushbutton [package="[SMD]"]  # not connected
  S37 = Pushbutton [package="[SMD]"]  # not connected
  S38 = Pushbutton [package="[SMD]"]  # not connected
  S39 = Pushbutton [package="[SMD]"]  # not connected
  S40 = Pushbutton [package="[SMD]"]  # not connected
  S41 = Pushbutton [package="[SMD]"]  # not connected
  S42 = Pushbutton [package="[SMD]"]  # not connected
  S43 = Pushbutton [package="[SMD]"]  # not connected
  S44 = Pushbutton [package="[SMD]"]  # not connected
  S45 = Pushbutton [package="[SMD]"]  # not connected
  S46 = Pushbutton [package="[SMD]"]  # not connected
  U9 = ENCODER-QUADRATURE [package=encoder-16mm-quad]  # not connected
  U10 = ENCODER-QUADRATURE [package=encoder-16mm-quad]  # not connected
  S47 = Pushbutton [package="[SMD]"]  # not connected
  S48 = Pushbutton [package="[SMD]"]  # not connected
  M5 = RioRand LM2596
  S49 = Momentary Switch [package=tactile_switch_smd]  # not connected
  S50 = Momentary Switch [package=tactile_switch_smd]  # not connected

nets:
  N1: J1.GND, M4.Pin_2, M5.Pin_2
  N2: J1.GNDBREAK, S27.L1
  N3: M4.Pin_1, S27.L2, M5.Pin_1
  N4: U8.VDD, M5.Pin_3
  N5: U8.VSS, M5.Pin_4
