# Fritzing sketch stereotaxic wiring v1 - reorganize - power switch (saved by Fritzing 1.0.4)
breadboards: 4

parts:
  S6 = Momentary Switch [package=ksa_sealed_tac_switch]
  S7 = Momentary Switch [package=ksa_sealed_tac_switch]
  S8 = Momentary Switch [package=ksa_sealed_tac_switch]
  S9 = Momentary Switch [package=ksa_sealed_tac_switch]
  S11 = Momentary Switch [package=ksa_sealed_tac_switch]
  S12 = Momentary Switch [package=ksa_sealed_tac_switch]
  S14 = Momentary Switch [package=ksa_sealed_tac_switch]
  S15 = Momentary Switch [package=ksa_sealed_tac_switch]
  S16 = Momentary Switch [package=ksa_sealed_tac_switch]
  S17 = Momentary Switch [package=ksa_sealed_tac_switch]
  S18 = Momentary Switch [package=ksa_sealed_tac_switch]
  S19 = Momentary Switch [package=ksa_sealed_tac_switch]
  S20 = Momentary Switch [package=ksa_sealed_tac_switch]
  J1 = Power Jack [package=power_jack_smd]
  U4 = SWITCH_SPDT [package=kps-1290]
  R53 = Resistor [tolerance=±5% power=0.25W resistance=100k package=THT]
  R54 = Resistor [tolerance=±5% power=0.25W resistance=100k package=THT]
  R55 = Resistor [tolerance=±5% power=0.25W resistance=100k package=THT]
  R56 = Resistor [tolerance=±5% power=0.25W resistance=100k package=THT]
  R57 = Resistor [tolerance=±5% power=0.25W resistance=100k package=THT]
  R58 = Resistor [tolerance=±5% power=0.25W resistance=100k package=THT]
  R59 = Resistor [tolerance=±5% power=0.25W resistance=100k package=THT]
  R60 = Resistor [tolerance=±5% power=0.25W resistance=100k package=THT]
  R61 = Resistor [tolerance=±5% power=0.25W resistance=100k package=THT]
  R62 = Resistor [tolerance=±5% power=0.25W resistance=100k package=THT]
  R63 = Resistor [tolerance=±5% power=0.25W resistance=100k package=THT]
  R64 = Resistor [tolerance=±5% power=0.25W resistance=100k package=THT]
  R65 = Resistor [tolerance=±5% power=0.25W resistance=100k package=THT]
  R67 = Resistor [tolerance=±5% power=0.25W resistance=100k package=THT]
  R68 = Resistor [tolerance=±5% power=0.25W resistance=100k package=THT]
  R69 = Resistor [tolerance=±5% power=0.25W resistance=10k package=THT]
  R70 = Resistor [tolerance=±5% power=0.25W resistance=10k package=THT]
  R71 = Resistor [tolerance=±5% power=0.25W resistance=10k package=THT]
  R72 = Resistor [tolerance=±5% power=0.25W resistance=10k package=THT]
  R73 = Resistor [tolerance=±5% power=0.25W resistance=10k package=THT]
  R74 = Resistor [tolerance=±5% power=0.25W resistance=10k package=THT]
  R75 = Resistor [tolerance=±5% power=0.25W resistance=10k package=THT]
  R76 = Resistor [tolerance=±5% power=0.25W resistance=10k package=THT]
  R77 = Resistor [tolerance=±5% power=0.25W resistance=10k package=THT]
  R78 = Resistor [tolerance=±5% power=0.25W resistance=10k package=THT]
  R79 = Resistor [tolerance=±5% power=0.25W resistance=10k package=THT]
  R80 = Resistor [tolerance=±5% power=0.25W resistance=10k package=THT]
  R81 = Resistor [tolerance=±5% power=0.25W resistance=10k package=THT]
  R82 = Resistor [tolerance=±5% power=0.25W resistance=10k package=THT]
  R83 = Resistor [tolerance=±5% power=0.25W resistance=10k package=THT]
  C17 = Ceramic Capacitor [capacitance=1µF voltage=50V package="100 mil [THT, multilayer]"]
  C18 = Ceramic Capacitor [capacitance=1µF voltage=50V package="100 mil [THT, multilayer]"]
  C19 = Ceramic Capacitor [capacitance=1µF voltage=50V package="100 mil [THT, multilayer]"]
  C20 = Ceramic Capacitor [capacitance=1µF voltage=50V package="100 mil [THT, multilayer]"]
  C21 = Ceramic Capacitor [capacitance=1µF voltage=50V package="100 mil [THT, multilayer]"]
  C22 = Ceramic Capacitor [capacitance=1µF voltage=50V package="100 mil [THT, multilayer]"]
  C23 = Ceramic Capacitor [capacitance=1µF voltage=50V package="100 mil [THT, multilayer]"]
  C24 = Ceramic Capacitor [capacitance=1µF voltage=50V package="100 mil [THT, multilayer]"]
  C25 = Ceramic Capacitor [capacitance=1µF voltage=50V package="100 mil [THT, multilayer]"]
  C26 = Ceramic Capacitor [capacitance=1µF voltage=50V package="100 mil [THT, multilayer]"]
  C27 = Ceramic Capacitor [capacitance=1µF voltage=50V package="100 mil [THT, multilayer]"]
  C28 = Ceramic Capacitor [capacitance=1µF voltage=50V package="100 mil [THT, multilayer]"]
  C29 = Ceramic Capacitor [capacitance=1µF voltage=50V package="100 mil [THT, multilayer]"]
  C30 = Ceramic Capacitor [capacitance=1µF voltage=50V package="100 mil [THT, multilayer]"]
  C31 = Ceramic Capacitor [capacitance=1µF voltage=50V package="100 mil [THT, multilayer]"]
  IC11 = Hex Inverter Schmitt Trigger SN74HC14 [package="DIP (Dual Inline)"]
  IC12 = Hex Inverter Schmitt Trigger SN74HC14 [package="DIP (Dual Inline)"]
  IC13 = Hex Inverter Schmitt Trigger SN74HC14 [package="DIP (Dual Inline)"]
  Raspberry_Pi_2 = Raspberry Pi 3 [part_number=RPI-3-V1.2]
  IC14 = SHIFT REGISTER [package=dil16]
  IC15 = SHIFT REGISTER [package=dil16]
  S21 = Momentary Switch [package=ksa_sealed_tac_switch]
  S22 = Momentary Switch [package=ksa_sealed_tac_switch]
  S23 = Momentary Switch [package=ksa_sealed_tac_switch]
  R84 = Resistor [tolerance=±5% power=0.25W resistance=100k package=THT]
  R85 = Resistor [tolerance=±5% power=0.25W resistance=100k package=THT]
  R86 = Resistor [tolerance=±5% power=0.25W resistance=100k package=THT]
  R87 = Resistor [tolerance=±5% power=0.25W resistance=10k package=THT]
  R88 = Resistor [tolerance=±5% power=0.25W resistance=10k package=THT]
  R89 = Resistor [tolerance=±5% power=0.25W resistance=10k package=THT]
  C32 = Ceramic Capacitor [capacitance=1µF voltage=50V package="100 mil [THT, multilayer]"]
  C33 = Ceramic Capacitor [capacitance=1µF voltage=50V package="100 mil [THT, multilayer]"]
  C34 = Ceramic Capacitor [capacitance=1µF voltage=50V package="100 mil [THT, multilayer]"]
  IC16 = Hex Inverter Schmitt Trigger SN74HC14 [package="DIP (Dual Inline)"]
  U5 = ENCODER-QUADRATURE [package=encoder-16mm-quad]
  U6 = ENCODER-QUADRATURE [package=encoder-16mm-quad]
  U7 = ENCODER-QUADRATURE [package=encoder-16mm-quad]
  R90 = Resistor [tolerance=±5% resistance=10k package="1206 [SMD]"]
  R91 = Resistor [tolerance=±5% resistance=10k package="1206 [SMD]"]
  R92 = Resistor [tolerance=±5% resistance=10k package="1206 [SMD]"]
  R93 = Resistor [tolerance=±5% resistance=10k package="1206 [SMD]"]
  R94 = Resistor [tolerance=±5% resistance=10k package="1206 [SMD]"]
  R95 = Resistor [tolerance=±5% resistance=10k package="1206 [SMD]"]
  Part4 = EasyDriver_v44
  Part5 = EasyDriver_v44
  Part6 = EasyDriver_v44
  M1 = Stepper Motor - Bipolar
  M2 = Stepper Motor - Bipolar
  M3 = Stepper Motor - Bipolar
  S24 = Toggle Switch [package=THT]
  S25 = Toggle Switch [package=THT]
  S26 = Toggle Switch [package=THT]
  C35 = Ceramic Capacitor [capacitance=100nF voltage=50V package="100 mil [THT, multilayer]"]
  C36 = Ceramic Capacitor [capacitance=100nF voltage=50V package="100 mil [THT, multilayer]"]
  C37 = Ceramic Capacitor [capacitance=100nF voltage=50V package="100 mil [THT, multilayer]"]
  C38 = Ceramic Capacitor [capacitance=100nF voltage=50V package="100 mil [THT, multilayer]"]
  C39 = Ceramic Capacitor [capacitance=100nF voltage=50V package="100 mil [THT, multilayer]"]
  C40 = Ceramic Capacitor [capacitance=100nF voltage=50V package="100 mil [THT, multilayer]"]
  R96 = Resistor [tolerance=±5% power=0.25W resistance=1k package=THT]
  R97 = Resistor [tolerance=±5% power=0.25W resistance=1k package=THT]
  R98 = Resistor [tolerance=±5% power=0.25W resistance=1k package=THT]
  R99 = Resistor [tolerance=±5% power=0.25W resistance=1k package=THT]
  R100 = Resistor [tolerance=±5% power=0.25W resistance=1k package=THT]
  R101 = Resistor [tolerance=±5% power=0.25W resistance=1k package=THT]
  M4 = RioRand LM2596  # not connected
  M5 = RioRand LM2596  # not connected
  S27 = Taiway 100-SP-X-T1 SPDT Miniature Toggle Switch [part_number=100-SP-X-T1-0-0-B1-M2 package=THT]  # not connected
  U8 = Graphical LCD 128x64 [package=lcd-g12864]  # not connected

nets (from the schematic view):
  N1: S6.2, R65.Pin_1, R81.Pin_0
  GND: S6.3, S7.3, S8.3, S9.3, S11.3, S12.3, S14.3, S15.3, S16.3, S17.3, S18.3, S19.3, S20.3, J1.GND, U4.P, C17.0, C18.0, C19.0, C20.0, C21.0, C22.0, C23.0, C24.0, C25.0, C26.0, C27.0, C28.0, C29.0, C30.0, C31.0, IC11.GND, IC12.GND, IC13.GND, Raspberry_Pi_2.GND, IC14.GND, IC14.ClkINH, IC15.GND, IC15.ClkINH, S21.3, S22.3, S23.3, C32.0, C33.0, C34.0, IC16.GND, U5.B, U6.B, U7.B, Part4.GND, Part5.GND, Part6.GND, S24.COM, S25.COM, S26.COM, C35.1, C36.0, C37.1, C38.0, C39.1, C40.0
  N2: S7.2, R58.Pin_1, R74.Pin_0
  N3: S8.2, R62.Pin_1, R78.Pin_0
  N4: S9.2, R64.Pin_1, R80.Pin_0
  N5: S11.2, R60.Pin_1, R76.Pin_0
  N6: S12.2, R61.Pin_1, R77.Pin_0
  N7: S14.2, R59.Pin_1, R75.Pin_0
  N8: S15.2, R63.Pin_1, R79.Pin_0
  N9: S16.2, R53.Pin_1, R69.Pin_0
  N10: S17.2, R54.Pin_1, R70.Pin_0
  N11: S18.2, R56.Pin_1, R72.Pin_0
  N12: S19.2, R55.Pin_1, R71.Pin_0
  N13: S20.2, R57.Pin_1, R73.Pin_0
  N14: U4.O, R67.Pin_1, R82.Pin_0
  N15: U4.S, R68.Pin_1, R83.Pin_0
  VCC: R53.Pin_0, R54.Pin_0, R55.Pin_0, R56.Pin_0, R57.Pin_0, R58.Pin_0, R59.Pin_0, R60.Pin_0, R61.Pin_0, R62.Pin_0, R63.Pin_0, R64.Pin_0, R65.Pin_0, R67.Pin_0, R68.Pin_0, IC11.VCC, IC12.VCC, IC13.VCC, Raspberry_Pi_2.3v3, Raspberry_Pi_2.3V3, IC14.VCC, IC15.VCC, R84.Pin_0, R85.Pin_0, R86.Pin_0, IC16.VCC, R90.Pin_0, R91.Pin_1, R92.Pin_0, R93.Pin_1, R94.Pin_0, R95.Pin_1
  N16: R69.Pin_1, C17.1, IC13.3A
  N17: R70.Pin_1, C18.1, IC13.2A
  N18: R71.Pin_1, C19.1, IC13.1A
  N19: R72.Pin_1, C20.1, IC12.3A
  N20: R73.Pin_1, C21.1, IC12.2A
  N21: R74.Pin_1, C22.1, IC12.1A
  N22: R75.Pin_1, C23.1, IC11.3A
  N23: R76.Pin_1, C24.1, IC11.2A
  N24: R77.Pin_1, C25.1, IC11.1A
  N25: R78.Pin_1, C26.1, IC11.6A
  N26: R79.Pin_1, C27.1, IC11.5A
  N27: R80.Pin_1, C28.1, IC11.4A
  N28: R81.Pin_1, C29.1, IC12.6A
  N29: R82.Pin_1, C30.1, IC12.5A
  N30: R83.Pin_1, C31.1, IC12.4A
  N31: IC11.1Y, IC15.H
  N32: IC11.2Y, IC15.G
  N33: IC11.3Y, IC15.F
  N34: IC11.4Y, IC15.D
  N35: IC11.5Y, IC15.C
  N36: IC11.6Y, IC15.B
  N37: IC12.1Y, IC15.E
  N38: IC12.2Y, IC14.H
  N39: IC12.3Y, IC14.G
  N40: IC12.4Y, IC14.C
  N41: IC12.5Y, IC14.B
  N42: IC12.6Y, IC14.A
  N43: IC13.1Y, IC14.F
  N44: IC13.2Y, IC14.E
  N45: IC13.3Y, IC14.D
  N46: IC13.4Y, Raspberry_Pi_2.GIPO26
  N47: IC13.4A, R89.Pin_1, C34.1
  N48: IC13.5Y, Raspberry_Pi_2.GIPO11
  N49: IC13.5A, R88.Pin_1, C33.1
  N50: IC13.6Y, Raspberry_Pi_2.GIPO10
  N51: IC13.6A, R87.Pin_1, C32.1
  N52: Raspberry_Pi_2.GPIO2, Part4.ENABLE, Part5.ENABLE, Part6.ENABLE
  N53: Raspberry_Pi_2.GPIO3, Part5.DIR
  N54: Raspberry_Pi_2.GIPO4, Part5.STEP
  N55: Raspberry_Pi_2.GIPO17, Part4.DIR
  N56: Raspberry_Pi_2.GIPO27, Part4.STEP
  N57: Raspberry_Pi_2.GIPO22, S26.L1
  N58: Raspberry_Pi_2.GIPO5, Part6.DIR
  N59: Raspberry_Pi_2.GIPO6, Part6.STEP
  N60: Raspberry_Pi_2.GIPO13, S25.L1
  N61: Raspberry_Pi_2.GIPO19, S24.L1
  N62: Raspberry_Pi_2.GIPO21, IC16.1Y
  N63: Raspberry_Pi_2.GIPO20, IC16.2Y
  N64: Raspberry_Pi_2.GIPO16, IC16.3Y
  N65: Raspberry_Pi_2.GIPO12, IC16.4Y
  N66: Raspberry_Pi_2.GIPO8, IC16.5Y
  N67: Raspberry_Pi_2.GIPO25, IC16.6Y
  N68: Raspberry_Pi_2.GIPO24, IC14.Qh
  N69: Raspberry_Pi_2.GIPO23, IC14.Clk, IC15.Clk
  VCC_2: Raspberry_Pi_2.5V, Part4.VCC, Part5.VCC, Part6.VCC
  N70: IC14.SH/LD, IC15.SH/LD
  N71: IC14.Ser, IC15.Qh
  N72: S21.2, R84.Pin_1, R87.Pin_0
  N73: S22.2, R85.Pin_1, R88.Pin_0
  N74: S23.2, R86.Pin_1, R89.Pin_0
  N75: IC16.1A, C38.1, R99.Pin_0
  N76: IC16.2A, C40.1, R101.Pin_0
  N77: IC16.3A, C39.0, R100.Pin_0
  N78: IC16.4A, C35.0, R96.Pin_0
  N79: IC16.5A, C36.1, R97.Pin_0
  N80: IC16.6A, C37.0, R98.Pin_0
  N81: U5.A, R91.Pin_0, R97.Pin_1
  N82: U5.C, R90.Pin_1, R96.Pin_1
  N83: U6.A, R93.Pin_0, R99.Pin_1
  N84: U6.C, R92.Pin_1, R98.Pin_1
  N85: U7.A, R95.Pin_0, R101.Pin_1
  N86: U7.C, R94.Pin_1, R100.Pin_1
  N87: Part4.V+, Part5.V+, Part6.V+
  N88: Part4.OUT2A, M2.A
  N89: Part4.OUT2B, M2.C
  N90: Part4.OUT1A, M2.B
  N91: Part4.OUT1B, M2.D
  N92: Part5.OUT2A, M1.A
  N93: Part5.OUT2B, M1.C
  N94: Part5.OUT1A, M1.B
  N95: Part5.OUT1B, M1.D
  N96: Part6.OUT2A, M3.A
  N97: Part6.OUT2B, M3.C
  N98: Part6.OUT1A, M3.B
  N99: Part6.OUT1B, M3.D

custom parts:
  SHIFT REGISTER: 8-bit SHIFT REGISTER, output latch
