# Fritzing sketch stereotaxic wiring v1 (saved by Fritzing 1.0.4)
breadboards: 6

parts:
  IC3 = Hex Inverter Schmitt Trigger SN74HC14 [package="DIP (Dual Inline)"]
  IC4 = SHIFT REGISTER [package=dil16]
  IC5 = SHIFT REGISTER [package=dil16]
  IC6 = Hex Inverter Schmitt Trigger SN74HC14 [package="DIP (Dual Inline)"]
  Raspberry_Pi_1 = Raspberry Pi 3 [part_number=RPI-3-V1.2]
  U1 = ENCODER-QUADRATURE [package=encoder-16mm-quad]
  U2 = ENCODER-QUADRATURE [package=encoder-16mm-quad]
  U3 = ENCODER-QUADRATURE [package=encoder-16mm-quad]
  S3 = Pushbutton [package="[THT]"]
  S4 = Pushbutton [package="[THT]"]
  S5 = Pushbutton [package="[THT]"]
  Part1 = EasyDriver_v44
  Part2 = EasyDriver_v44
  Part3 = EasyDriver_v44
  S6 = Momentary Switch [package=ksa_sealed_tac_switch]
  S7 = Momentary Switch [package=ksa_sealed_tac_switch]
  S8 = Momentary Switch [package=ksa_sealed_tac_switch]
  S9 = Momentary Switch [package=ksa_sealed_tac_switch]
  S10 = Momentary Switch [package=ksa_sealed_tac_switch]
  S11 = Momentary Switch [package=ksa_sealed_tac_switch]
  S12 = Momentary Switch [package=ksa_sealed_tac_switch]
  S13 = Momentary Switch [package=ksa_sealed_tac_switch]
  S14 = Momentary Switch [package=ksa_sealed_tac_switch]
  S15 = Momentary Switch [package=ksa_sealed_tac_switch]
  S16 = Momentary Switch [package=ksa_sealed_tac_switch]
  S17 = Momentary Switch [package=ksa_sealed_tac_switch]
  S18 = Momentary Switch [package=ksa_sealed_tac_switch]
  S19 = Momentary Switch [package=ksa_sealed_tac_switch]
  S20 = Momentary Switch [package=ksa_sealed_tac_switch]
  IC7 = Hex Inverter Schmitt Trigger SN74HC14 [package="DIP (Dual Inline)"]
  R4 = Resistor [tolerance=±5% resistance=10k package="1206 [SMD]"]
  R5 = Resistor [tolerance=±5% resistance=10k package="1206 [SMD]"]
  R6 = Resistor [tolerance=±5% resistance=10k package="1206 [SMD]"]
  R7 = Resistor [tolerance=±5% power=0.25W resistance=10k package=THT]
  R8 = Resistor [tolerance=±5% power=0.25W resistance=10k package=THT]
  R9 = Resistor [tolerance=±5% power=0.25W resistance=10k package=THT]
  R10 = Resistor [tolerance=±5% power=0.25W resistance=10k package=THT]
  R11 = Resistor [tolerance=±5% power=0.25W resistance=10k package=THT]
  R12 = Resistor [tolerance=±5% power=0.25W resistance=10k package=THT]
  R13 = Resistor [tolerance=±5% power=0.25W resistance=10k package=THT]
  R14 = Resistor [tolerance=±5% power=0.25W resistance=10k package=THT]
  R15 = Resistor [tolerance=±5% power=0.25W resistance=10k package=THT]
  R16 = Resistor [tolerance=±5% power=0.25W resistance=10k package=THT]
  R17 = Resistor [tolerance=±5% power=0.25W resistance=10k package=THT]
  R18 = Resistor [tolerance=±5% power=0.25W resistance=10k package=THT]
  R19 = Resistor [tolerance=±5% power=0.25W resistance=10k package=THT]
  R20 = Resistor [tolerance=±5% power=0.25W resistance=10k package=THT]
  R21 = Resistor [tolerance=±5% power=0.25W resistance=10k package=THT]
  R22 = Resistor [tolerance=±5% power=0.25W resistance=1k package=THT]
  R23 = Resistor [tolerance=±5% power=0.25W resistance=1k package=THT]
  R24 = Resistor [tolerance=±5% power=0.25W resistance=1k package=THT]
  R25 = Resistor [tolerance=±5% power=0.25W resistance=1k package=THT]
  R26 = Resistor [tolerance=±5% power=0.25W resistance=1k package=THT]
  R27 = Resistor [tolerance=±5% power=0.25W resistance=1k package=THT]
  R28 = Resistor [tolerance=±5% power=0.25W resistance=1k package=THT]
  R29 = Resistor [tolerance=±5% power=0.25W resistance=1k package=THT]
  R30 = Resistor [tolerance=±5% power=0.25W resistance=1k package=THT]
  R31 = Resistor [tolerance=±5% power=0.25W resistance=1k package=THT]
  R32 = Resistor [tolerance=±5% power=0.25W resistance=1k package=THT]
  R33 = Resistor [tolerance=±5% power=0.25W resistance=1k package=THT]
  R34 = Resistor [tolerance=±5% power=0.25W resistance=1k package=THT]
  R35 = Resistor [tolerance=±5% power=0.25W resistance=1k package=THT]
  R36 = Resistor [tolerance=±5% power=0.25W resistance=1k package=THT]
  C2 = Ceramic Capacitor [capacitance=10µF voltage=35V package="100 mil [THT, multilayer]"]
  C3 = Ceramic Capacitor [capacitance=10µF voltage=35V package="100 mil [THT, multilayer]"]
  C4 = Ceramic Capacitor [capacitance=10µF voltage=35V package="100 mil [THT, multilayer]"]
  C5 = Ceramic Capacitor [capacitance=10µF voltage=35V package="100 mil [THT, multilayer]"]
  C6 = Ceramic Capacitor [capacitance=10µF voltage=35V package="100 mil [THT, multilayer]"]
  C7 = Ceramic Capacitor [capacitance=10µF voltage=35V package="100 mil [THT, multilayer]"]
  C8 = Ceramic Capacitor [capacitance=10µF voltage=35V package="100 mil [THT, multilayer]"]
  C9 = Ceramic Capacitor [capacitance=10µF voltage=35V package="100 mil [THT, multilayer]"]
  C10 = Ceramic Capacitor [capacitance=10µF voltage=35V package="100 mil [THT, multilayer]"]
  C11 = Ceramic Capacitor [capacitance=10µF voltage=35V package="100 mil [THT, multilayer]"]
  C12 = Ceramic Capacitor [capacitance=10µF voltage=35V package="100 mil [THT, multilayer]"]
  C13 = Ceramic Capacitor [capacitance=10µF voltage=35V package="100 mil [THT, multilayer]"]
  C14 = Ceramic Capacitor [capacitance=10µF voltage=35V package="100 mil [THT, multilayer]"]
  C15 = Ceramic Capacitor [capacitance=10µF voltage=35V package="100 mil [THT, multilayer]"]
  C16 = Ceramic Capacitor [capacitance=10µF voltage=35V package="100 mil [THT, multilayer]"]
  IC8 = Hex Inverter Schmitt Trigger SN74HC14 [package="DIP (Dual Inline)"]
  R37 = Resistor [tolerance=±5% resistance=10k package="1206 [SMD]"]
  R38 = Resistor [tolerance=±5% resistance=10k package="1206 [SMD]"]
  R39 = Resistor [tolerance=±5% resistance=10k package="1206 [SMD]"]
  J1 = Power Jack [package=power_jack_smd]

nets (from the breadboard view):
  N1: IC3.1A, R28.Pin_0, C8.0
  N2: IC3.1Y, IC5.QD
  N3: IC3.2A, R29.Pin_0, C9.0
  N4: IC3.2Y, IC5.QE
  N5: IC3.3A, R30.Pin_0, C10.0
  N6: IC3.3Y, IC5.QF
  GND: IC3.GND, IC4.GND, IC4.QA, IC5.GND, IC5.QA, IC6.GND, Raspberry_Pi_1.GND, IC7.GND
  N7: IC3.4Y, IC5.G
  N8: IC3.4A, R25.Pin_0, C5.0
  N9: IC3.5Y, IC5.SER
  N10: IC3.5A, R26.Pin_0, C6.0
  N11: IC3.6Y, IC5.QG
  N12: IC3.6A, R27.Pin_0, C7.0
  VCC: IC3.VCC, IC4.VCC, IC5.VCC, IC6.VCC, Raspberry_Pi_1.3v3, Raspberry_Pi_1.3V3, IC7.VCC, IC8.VCC
  N13: IC4.QD, IC6.1Y
  N14: IC4.QE, IC6.2Y
  N15: IC4.QF, IC6.3Y
  N16: IC4.QG, IC6.4Y
  N17: IC4.QH*, IC5.SCL
  N18: IC4.RCK, IC7.3Y
  N19: IC4.G, IC7.2Y
  N20: IC4.SER, IC7.1Y
  N21: IC5.QB, Raspberry_Pi_1.GIPO18
  N22: IC5.QC, Raspberry_Pi_1.GIPO23
  N23: IC5.QH*, Raspberry_Pi_1.GIPO24
  N24: IC5.SCK, IC6.5Y
  N25: IC5.RCK, IC6.6Y
  N26: IC6.1A, R31.Pin_0, C11.0
  N27: IC6.2A, R32.Pin_0, C12.0
  N28: IC6.3A, R33.Pin_0, C13.0
  N29: IC6.4A, R22.Pin_0, C3.0
  N30: IC6.5A, R23.Pin_0, C2.0
  N31: IC6.6A, R24.Pin_0, C4.0
  N32: Raspberry_Pi_1.GPIO2, Part3.ENABLE
  N33: Raspberry_Pi_1.GPIO3, Part1.DIR
  N34: Raspberry_Pi_1.GIPO4, Part1.STEP
  N35: Raspberry_Pi_1.GIPO17, Part2.DIR
  N36: Raspberry_Pi_1.GIPO27, Part2.STEP
  N37: Raspberry_Pi_1.GIPO10, Raspberry_Pi_1.GIPO11, Raspberry_Pi_1.GIPO26, U1.B, U2.B, U3.B, S3.Pin_1, S3.Pin_2, S4.Pin_1, S4.Pin_2, S5.Pin_1, S5.Pin_2, S6.1, S7.1, S8.1, S9.1, S10.1, S11.1, S12.1, S13.1, S14.1, S15.1, S16.1, S17.1, S18.1, S19.1, S20.1, C2.1, C3.1, C4.1, C5.1, C6.1, C7.1, C8.1, C9.1, C10.1, C11.1, C12.1, C13.1, C14.1, C15.1, C16.1
  N38: Raspberry_Pi_1.ID_SD, Part3.DIR
  N39: Raspberry_Pi_1.GIPO5, Part3.STEP
  N40: Raspberry_Pi_1.GIPO21, IC8.1Y
  N41: Raspberry_Pi_1.GIPO20, IC8.4Y
  N42: Raspberry_Pi_1.GIPO16, IC8.2Y
  N43: Raspberry_Pi_1.GIPO12, IC8.5Y
  N44: Raspberry_Pi_1.GIPO8, IC8.3Y
  N45: Raspberry_Pi_1.GIPO25, IC8.6Y
  5V: Raspberry_Pi_1.5V, Part3.VCC
  N46: U1.A, R6.Pin_0, IC8.3A
  N47: U1.C, R5.Pin_1, IC8.2A
  N48: U2.A, IC8.5A, R38.Pin_0
  N49: U2.C, IC8.6A, R39.Pin_1
  N50: U3.A, R4.Pin_0, IC8.1A
  N51: U3.C, IC8.4A, R37.Pin_1
  N52: S3.Pin_3, S3.Pin_4
  N53: S4.Pin_3, S4.Pin_4
  N54: S5.Pin_3, S5.Pin_4
  GND_2: Part1.GND, Part2.GND, Part3.GND, IC8.GND, J1.GND
  N55: Part1.V+, Part2.V+, Part3.V+, J1.PWR
  N56: S6.2, R9.Pin_0, R24.Pin_1
  N57: S7.2, R16.Pin_0, R31.Pin_1
  N58: S8.2, R12.Pin_0, R27.Pin_1
  N59: S9.2, R10.Pin_0, R25.Pin_1
  N60: S10.2, R7.Pin_0, R22.Pin_1
  N61: S11.2, R14.Pin_0, R29.Pin_1
  N62: S12.2, R13.Pin_0, R28.Pin_1
  N63: S13.2, R8.Pin_0, R23.Pin_1
  N64: S14.2, R15.Pin_0, R30.Pin_1
  N65: S15.2, R11.Pin_0, R26.Pin_1
  N66: S16.2, R21.Pin_0, R36.Pin_1
  N67: S17.2, R20.Pin_0, R35.Pin_1
  N68: S18.2, R18.Pin_0, R33.Pin_1
  N69: S19.2, R19.Pin_0, R34.Pin_1
  N70: S20.2, R17.Pin_0, R32.Pin_1
  N71: IC7.1A, R34.Pin_0, C14.0
  N72: IC7.2A, R35.Pin_0, C15.0
  N73: IC7.3A, R36.Pin_0, C16.0
  N74: R4.Pin_1, R5.Pin_0, R6.Pin_1, R7.Pin_1, R8.Pin_1, R9.Pin_1, R10.Pin_1, R11.Pin_1, R12.Pin_1, R13.Pin_1, R14.Pin_1, R15.Pin_1, R16.Pin_1, R17.Pin_1, R18.Pin_1, R19.Pin_1, R20.Pin_1, R21.Pin_1, R37.Pin_0, R38.Pin_1, R39.Pin_0
