# Fritzing sketch stereotaxic wiring v2b - gerber (saved by Fritzing 1.0.4)
circuit board: 20.4cm x 17.7987cm

parts:
  Shift1 = SHIFT REGISTER [package=dil16]
  Shift2 = SHIFT REGISTER [package=dil16]
  Shift3 = SHIFT REGISTER [package=dil16]
  Shift4 = SHIFT REGISTER [package=dil16]
  S_Trig1 = Hex Inverter Schmitt Trigger SN74HC14 [package="DIP (Dual Inline)"]
  S_Trig2 = Hex Inverter Schmitt Trigger SN74HC14 [package="DIP (Dual Inline)"]
  S_Trig4 = Hex Inverter Schmitt Trigger SN74HC14 [package="DIP (Dual Inline)"]
  S_Trig5 = Hex Inverter Schmitt Trigger SN74HC14 [package="DIP (Dual Inline)"]
  S_Trig6 = Hex Inverter Schmitt Trigger SN74HC14 [package="DIP (Dual Inline)"]
  S_Trig7 = Hex Inverter Schmitt Trigger SN74HC14 [package="DIP (Dual Inline)"]
  S_Trig8 = Hex Inverter Schmitt Trigger SN74HC14 [package="DIP (Dual Inline)"]
  1uF_cap_1 = Ceramic Capacitor [capacitance=1µF voltage=35V package="100 mil [THT, multilayer]"]
  1uF_cap_2 = Ceramic Capacitor [capacitance=1µF voltage=50V package="100 mil [THT, multilayer]"]
  1uF_cap_3 = Ceramic Capacitor [capacitance=1µF voltage=50V package="100 mil [THT, multilayer]"]
  1uF_cap_4 = Ceramic Capacitor [capacitance=1µF voltage=50V package="100 mil [THT, multilayer]"]
  1uF_cap_5 = Ceramic Capacitor [capacitance=1µF voltage=50V package="100 mil [THT, multilayer]"]
  1uF_cap_6 = Ceramic Capacitor [capacitance=1µF voltage=50V package="100 mil [THT, multilayer]"]
  1uF_cap_7 = Ceramic Capacitor [capacitance=1µF voltage=50V package="100 mil [THT, multilayer]"]
  1uF_cap_8 = Ceramic Capacitor [capacitance=1µF voltage=50V package="100 mil [THT, multilayer]"]
  1uF_cap_9 = Ceramic Capacitor [capacitance=1µF voltage=50V package="100 mil [THT, multilayer]"]
  1uF_cap_10 = Ceramic Capacitor [capacitance=1µF voltage=50V package="100 mil [THT, multilayer]"]
  1uF_cap_11 = Ceramic Capacitor [capacitance=1µF voltage=50V package="100 mil [THT, multilayer]"]
  1uF_cap_12 = Ceramic Capacitor [capacitance=1µF voltage=50V package="100 mil [THT, multilayer]"]
  1uF_cap_24 = Ceramic Capacitor [capacitance=1µF voltage=50V package="100 mil [THT, multilayer]"]
  1uF_cap_23 = Ceramic Capacitor [capacitance=1µF voltage=50V package="100 mil [THT, multilayer]"]
  1uF_cap_22 = Ceramic Capacitor [capacitance=1µF voltage=50V package="100 mil [THT, multilayer]"]
  1uF_cap_21 = Ceramic Capacitor [capacitance=1µF voltage=50V package="100 mil [THT, multilayer]"]
  1uF_cap_20 = Ceramic Capacitor [capacitance=1µF voltage=50V package="100 mil [THT, multilayer]"]
  1uF_cap_19 = Ceramic Capacitor [capacitance=1µF voltage=50V package="100 mil [THT, multilayer]"]
  1uF_cap_18 = Ceramic Capacitor [capacitance=1µF voltage=50V package="100 mil [THT, multilayer]"]
  1uF_cap_17 = Ceramic Capacitor [capacitance=1µF voltage=50V package="100 mil [THT, multilayer]"]
  1uF_cap_16 = Ceramic Capacitor [capacitance=1µF voltage=50V package="100 mil [THT, multilayer]"]
  1uF_cap_15 = Ceramic Capacitor [capacitance=1µF voltage=50V package="100 mil [THT, multilayer]"]
  1uF_cap_14 = Ceramic Capacitor [capacitance=1µF voltage=50V package="100 mil [THT, multilayer]"]
  1uF_cap_13 = Ceramic Capacitor [capacitance=1µF voltage=50V package="100 mil [THT, multilayer]"]
  1uF_cap_25 = Ceramic Capacitor [capacitance=1µF voltage=50V package="100 mil [THT, multilayer]"]
  1uF_cap_26 = Ceramic Capacitor [capacitance=1µF voltage=50V package="100 mil [THT, multilayer]"]
  1uF_cap_36 = Ceramic Capacitor [capacitance=1µF voltage=50V package="100 mil [THT, multilayer]"]
  1uF_cap_27 = Ceramic Capacitor [capacitance=1µF voltage=50V package="100 mil [THT, multilayer]"]
  1uF_cap_28 = Ceramic Capacitor [capacitance=1µF voltage=50V package="100 mil [THT, multilayer]"]
  1uF_cap_29 = Ceramic Capacitor [capacitance=1µF voltage=50V package="100 mil [THT, multilayer]"]
  1uF_cap_30 = Ceramic Capacitor [capacitance=1µF voltage=50V package="100 mil [THT, multilayer]"]
  1uF_cap_31 = Ceramic Capacitor [capacitance=1µF voltage=50V package="100 mil [THT, multilayer]"]
  1uF_cap_32 = Ceramic Capacitor [capacitance=1µF voltage=50V package="100 mil [THT, multilayer]"]
  1uF_cap_33 = Ceramic Capacitor [capacitance=1µF voltage=50V package="100 mil [THT, multilayer]"]
  1uF_cap_34 = Ceramic Capacitor [capacitance=1µF voltage=50V package="100 mil [THT, multilayer]"]
  1uF_cap_35 = Ceramic Capacitor [capacitance=1µF voltage=50V package="100 mil [THT, multilayer]"]
  1uF_cap_37 = Ceramic Capacitor [capacitance=1µF voltage=50V package="100 mil [THT, multilayer]"]
  1uF_cap_38 = Ceramic Capacitor [capacitance=1µF voltage=50V package="100 mil [THT, multilayer]"]
  1uF_cap_39 = Ceramic Capacitor [capacitance=1µF voltage=50V package="100 mil [THT, multilayer]"]
  1uF_cap_40 = Ceramic Capacitor [capacitance=1µF voltage=50V package="100 mil [THT, multilayer]"]
  1uF_cap_41 = Ceramic Capacitor [capacitance=1µF voltage=50V package="100 mil [THT, multilayer]"]
  1uF_cap_42 = Ceramic Capacitor [capacitance=1µF voltage=50V package="100 mil [THT, multilayer]"]
  1uF_cap_43 = Ceramic Capacitor [capacitance=1µF voltage=50V package="100 mil [THT, multilayer]"]
  1uF_cap_44 = Ceramic Capacitor [capacitance=1µF voltage=50V package="100 mil [THT, multilayer]"]
  1uF_cap_45 = Ceramic Capacitor [capacitance=1µF voltage=50V package="100 mil [THT, multilayer]"]
  1uF_cap_46 = Ceramic Capacitor [capacitance=1µF voltage=50V package="100 mil [THT, multilayer]"]
  1uF_cap_47 = Ceramic Capacitor [capacitance=1µF voltage=50V package="100 mil [THT, multilayer]"]
  1uF_cap_48 = Ceramic Capacitor [capacitance=1µF voltage=50V package="100 mil [THT, multilayer]"]
  10kOhm_R1 = Resistor [tolerance=±5% resistance=10k power=0.25W package=THT]
  10kOhm_R2 = Resistor [tolerance=±5% resistance=10k power=0.25W package=THT]
  10kOhm_R3 = Resistor [tolerance=±5% resistance=10k power=0.25W package=THT]
  10kOhm_R4 = Resistor [tolerance=±5% resistance=10k power=0.25W package=THT]
  10kOhm_R5 = Resistor [tolerance=±5% resistance=10k power=0.25W package=THT]
  10kOhm_R6 = Resistor [tolerance=±5% resistance=10k power=0.25W package=THT]
  10kOhm_R7 = Resistor [tolerance=±5% resistance=10k power=0.25W package=THT]
  10kOhm_R8 = Resistor [tolerance=±5% resistance=10k power=0.25W package=THT]
  10kOhm_R9 = Resistor [tolerance=±5% resistance=10k power=0.25W package=THT]
  10kOhm_R10 = Resistor [tolerance=±5% resistance=10k power=0.25W package=THT]
  10kOhm_R11 = Resistor [tolerance=±5% resistance=10k power=0.25W package=THT]
  10kOhm_R12 = Resistor [tolerance=±5% resistance=10k power=0.25W package=THT]
  10kOhm_R13 = Resistor [tolerance=±5% resistance=10k power=0.25W package=THT]
  10kOhm_R14 = Resistor [tolerance=±5% resistance=10k power=0.25W package=THT]
  10kOhm_R15 = Resistor [tolerance=±5% resistance=10k power=0.25W package=THT]
  10kOhm_R16 = Resistor [tolerance=±5% resistance=10k power=0.25W package=THT]
  10kOhm_R17 = Resistor [tolerance=±5% resistance=10k power=0.25W package=THT]
  10kOhm_R18 = Resistor [tolerance=±5% resistance=10k power=0.25W package=THT]
  10kOhm_R19 = Resistor [tolerance=±5% resistance=10k power=0.25W package=THT]
  10kOhm_R20 = Resistor [tolerance=±5% resistance=10k power=0.25W package=THT]
  10kOhm_R21 = Resistor [tolerance=±5% resistance=10k power=0.25W package=THT]
  10kOhm_R22 = Resistor [tolerance=±5% resistance=10k power=0.25W package=THT]
  10kOhm_R23 = Resistor [tolerance=±5% resistance=10k power=0.25W package=THT]
  10kOhm_R24 = Resistor [tolerance=±5% resistance=10k power=0.25W package=THT]
  10kOhm_R25 = Resistor [tolerance=±5% resistance=10k power=0.25W package=THT]
  10kOhm_R26 = Resistor [tolerance=±5% resistance=10k power=0.25W package=THT]
  10kOhm_R27 = Resistor [tolerance=±5% resistance=10k power=0.25W package=THT]
  10kOhm_R28 = Resistor [tolerance=±5% resistance=10k power=0.25W package=THT]
  10kOhm_R29 = Resistor [tolerance=±5% resistance=10k power=0.25W package=THT]
  10kOhm_R30 = Resistor [tolerance=±5% resistance=10k power=0.25W package=THT]
  10kOhm_R31 = Resistor [tolerance=±5% resistance=10k power=0.25W package=THT]
  10kOhm_R32 = Resistor [tolerance=±5% resistance=10k power=0.25W package=THT]
  10kOhm_R33 = Resistor [tolerance=±5% resistance=10k power=0.25W package=THT]
  10kOhm_R34 = Resistor [tolerance=±5% resistance=10k power=0.25W package=THT]
  10kOhm_R35 = Resistor [tolerance=±5% resistance=10k power=0.25W package=THT]
  10kOhm_R36 = Resistor [tolerance=±5% resistance=10k power=0.25W package=THT]
  10kOhm_R37 = Resistor [tolerance=±5% resistance=10k power=0.25W package=THT]
  10kOhm_R38 = Resistor [tolerance=±5% resistance=10k power=0.25W package=THT]
  10kOhm_R39 = Resistor [tolerance=±5% resistance=10k power=0.25W package=THT]
  10kOhm_R40 = Resistor [tolerance=±5% resistance=10k power=0.25W package=THT]
  10kOhm_R41 = Resistor [tolerance=±5% resistance=10k power=0.25W package=THT]
  10kOhm_R42 = Resistor [tolerance=±5% resistance=10k power=0.25W package=THT]
  10kOhm_R43 = Resistor [tolerance=±5% resistance=10k power=0.25W package=THT]
  10kOhm_R44 = Resistor [tolerance=±5% resistance=10k power=0.25W package=THT]
  10kOhm_R45 = Resistor [tolerance=±5% resistance=10k power=0.25W package=THT]
  10kOhm_R46 = Resistor [tolerance=±5% resistance=10k power=0.25W package=THT]
  10kOhm_R47 = Resistor [tolerance=±5% resistance=10k power=0.25W package=THT]
  100kOhm_R1 = Resistor [tolerance=±5% resistance=100k power=0.25W package=THT]
  100kOhm_R2 = Resistor [tolerance=±5% resistance=100k power=0.25W package=THT]
  100kOhm_R3 = Resistor [tolerance=±5% resistance=100k power=0.25W package=THT]
  100kOhm_R4 = Resistor [tolerance=±5% resistance=100k power=0.25W package=THT]
  100kOhm_R5 = Resistor [tolerance=±5% resistance=100k power=0.25W package=THT]
  100kOhm_R6 = Resistor [tolerance=±5% resistance=100k power=0.25W package=THT]
  100kOhm_R7 = Resistor [tolerance=±5% resistance=100k power=0.25W package=THT]
  100kOhm_R8 = Resistor [tolerance=±5% resistance=100k power=0.25W package=THT]
  100kOhm_R9 = Resistor [tolerance=±5% resistance=100k power=0.25W package=THT]
  100kOhm_R10 = Resistor [tolerance=±5% resistance=100k power=0.25W package=THT]
  100kOhm_R11 = Resistor [tolerance=±5% resistance=100k power=0.25W package=THT]
  100kOhm_R12 = Resistor [tolerance=±5% resistance=100k power=0.25W package=THT]
  100kOhm_R13 = Resistor [tolerance=±5% resistance=100k power=0.25W package=THT]
  100kOhm_R14 = Resistor [tolerance=±5% resistance=100k power=0.25W package=THT]
  100kOhm_R15 = Resistor [tolerance=±5% resistance=100k power=0.25W package=THT]
  100kOhm_R16 = Resistor [tolerance=±5% resistance=100k power=0.25W package=THT]
  100kOhm_R17 = Resistor [tolerance=±5% resistance=100k power=0.25W package=THT]
  100kOhm_R18 = Resistor [tolerance=±5% resistance=100k power=0.25W package=THT]
  100kOhm_R19 = Resistor [tolerance=±5% resistance=100k power=0.25W package=THT]
  100kOhm_R20 = Resistor [tolerance=±5% resistance=100k power=0.25W package=THT]
  100kOhm_R21 = Resistor [tolerance=±5% resistance=100k power=0.25W package=THT]
  100kOhm_R22 = Resistor [tolerance=±5% resistance=100k power=0.25W package=THT]
  100kOhm_R23 = Resistor [tolerance=±5% resistance=100k power=0.25W package=THT]
  100kOhm_R24 = Resistor [tolerance=±5% resistance=100k power=0.25W package=THT]
  100kOhm_R25 = Resistor [tolerance=±5% resistance=100k power=0.25W package=THT]
  100kOhm_R26 = Resistor [tolerance=±5% resistance=100k power=0.25W package=THT]
  100kOhm_R27 = Resistor [tolerance=±5% resistance=100k power=0.25W package=THT]
  100kOhm_R28 = Resistor [tolerance=±5% resistance=100k power=0.25W package=THT]
  100kOhm_R29 = Resistor [tolerance=±5% resistance=100k power=0.25W package=THT]
  100kOhm_R30 = Resistor [tolerance=±5% resistance=100k power=0.25W package=THT]
  100kOhm_R31 = Resistor [tolerance=±5% resistance=100k power=0.25W package=THT]
  100kOhm_R32 = Resistor [tolerance=±5% resistance=100k power=0.25W package=THT]
  100kOhm_R33 = Resistor [tolerance=±5% resistance=100k power=0.25W package=THT]
  100kOhm_R34 = Resistor [tolerance=±5% resistance=100k power=0.25W package=THT]
  100kOhm_R35 = Resistor [tolerance=±5% resistance=100k power=0.25W package=THT]
  100kOhm_R36 = Resistor [tolerance=±5% resistance=100k power=0.25W package=THT]
  100kOhm_R37 = Resistor [tolerance=±5% resistance=100k power=0.25W package=THT]
  100kOhm_R38 = Resistor [tolerance=±5% resistance=100k power=0.25W package=THT]
  100kOhm_R39 = Resistor [tolerance=±5% resistance=100k power=0.25W package=THT]
  100kOhm_R40 = Resistor [tolerance=±5% resistance=100k power=0.25W package=THT]
  100kOhm_R41 = Resistor [tolerance=±5% resistance=100k power=0.25W package=THT]
  100kOhm_R42 = Resistor [tolerance=±5% resistance=100k power=0.25W package=THT]
  100kOhm_R43 = Resistor [tolerance=±5% resistance=100k power=0.25W package=THT]
  100kOhm_R44 = Resistor [tolerance=±5% resistance=100k power=0.25W package=THT]
  100kOhm_R45 = Resistor [tolerance=±5% resistance=100k power=0.25W package=THT]
  100kOhm_R46 = Resistor [tolerance=±5% resistance=100k power=0.25W package=THT]
  100kOhm_R47 = Resistor [tolerance=±5% resistance=100k power=0.25W package=THT]
  100kOhm_R48 = Resistor [tolerance=±5% resistance=100k power=0.25W package=THT]
  10kOhm_R48 = Resistor [tolerance=±5% power=0.25W resistance=10k package=THT]
  S_Trig3 = Hex Inverter Schmitt Trigger SN74HC14 [package="DIP (Dual Inline)"]

nets:
  N1: Shift1.SH/LD, Shift2.SH/LD, Shift3.SH/LD, Shift4.SH/LD
  N2: Shift1.Clk, Shift2.Clk, Shift3.Clk, Shift4.Clk
  N3: Shift1.E, S_Trig1.6Y
  N4: Shift1.F, S_Trig1.5Y
  N5: Shift1.G, S_Trig1.4Y
  N6: Shift1.H, S_Trig1.1Y
  GND: Shift1.GND, Shift2.GND, Shift3.GND, Shift4.GND, S_Trig1.GND, S_Trig2.GND, S_Trig4.GND, S_Trig5.GND, S_Trig6.GND, S_Trig7.GND, S_Trig8.GND, 1uF_cap_1.0, 1uF_cap_2.0, 1uF_cap_3.0, 1uF_cap_4.0, 1uF_cap_5.0, 1uF_cap_6.0, 1uF_cap_7.0, 1uF_cap_8.0, 1uF_cap_9.0, 1uF_cap_10.0, 1uF_cap_11.0, 1uF_cap_12.0, 1uF_cap_24.0, 1uF_cap_23.0, 1uF_cap_22.0, 1uF_cap_21.0, 1uF_cap_20.0, 1uF_cap_19.0, 1uF_cap_18.0, 1uF_cap_17.0, 1uF_cap_16.0, 1uF_cap_15.0, 1uF_cap_14.0, 1uF_cap_13.0, 1uF_cap_25.1, 1uF_cap_26.1, 1uF_cap_36.1, 1uF_cap_27.1, 1uF_cap_28.1, 1uF_cap_29.1, 1uF_cap_30.1, 1uF_cap_31.1, 1uF_cap_32.1, 1uF_cap_33.1, 1uF_cap_34.1, 1uF_cap_35.1, 1uF_cap_37.1, 1uF_cap_38.1, 1uF_cap_39.1, 1uF_cap_40.1, 1uF_cap_41.1, 1uF_cap_42.1, 1uF_cap_43.1, 1uF_cap_44.1, 1uF_cap_45.1, 1uF_cap_46.1, 1uF_cap_47.1, 1uF_cap_48.1, S_Trig3.GND
  N7: Shift1.Ser, Shift2.Qh
  N8: Shift1.A, S_Trig5.6Y
  N9: Shift1.B, S_Trig5.3Y
  N10: Shift1.C, S_Trig5.2Y
  N11: Shift1.D, S_Trig5.1Y
  VCC: Shift1.VCC, Shift2.VCC, Shift3.VCC, Shift4.VCC, S_Trig1.VCC, S_Trig2.VCC, S_Trig4.VCC, S_Trig5.VCC, S_Trig6.VCC, S_Trig7.VCC, S_Trig8.VCC, 100kOhm_R1.Pin_1, 100kOhm_R2.Pin_1, 100kOhm_R3.Pin_1, 100kOhm_R4.Pin_1, 100kOhm_R5.Pin_1, 100kOhm_R6.Pin_1, 100kOhm_R7.Pin_1, 100kOhm_R8.Pin_1, 100kOhm_R9.Pin_1, 100kOhm_R10.Pin_1, 100kOhm_R11.Pin_1, 100kOhm_R12.Pin_1, 100kOhm_R13.Pin_1, 100kOhm_R14.Pin_1, 100kOhm_R15.Pin_1, 100kOhm_R16.Pin_1, 100kOhm_R17.Pin_1, 100kOhm_R18.Pin_1, 100kOhm_R19.Pin_1, 100kOhm_R20.Pin_1, 100kOhm_R21.Pin_1, 100kOhm_R22.Pin_1, 100kOhm_R23.Pin_1, 100kOhm_R24.Pin_1, 100kOhm_R25.Pin_0, 100kOhm_R26.Pin_0, 100kOhm_R27.Pin_0, 100kOhm_R28.Pin_0, 100kOhm_R29.Pin_0, 100kOhm_R30.Pin_0, 100kOhm_R31.Pin_0, 100kOhm_R32.Pin_0, 100kOhm_R33.Pin_0, 100kOhm_R34.Pin_0, 100kOhm_R35.Pin_0, 100kOhm_R36.Pin_0, 100kOhm_R37.Pin_0, 100kOhm_R38.Pin_0, 100kOhm_R39.Pin_0, 100kOhm_R40.Pin_0, 100kOhm_R41.Pin_0, 100kOhm_R42.Pin_0, 100kOhm_R43.Pin_0, 100kOhm_R44.Pin_0, 100kOhm_R45.Pin_0, 100kOhm_R46.Pin_0, 100kOhm_R47.Pin_0, 100kOhm_R48.Pin_0, S_Trig3.VCC
  N12: Shift2.E, S_Trig1.3Y
  N13: Shift2.F, S_Trig1.2Y
  N14: Shift2.G, S_Trig2.1Y
  N15: Shift2.H, S_Trig2.2Y
  N16: Shift2.Ser, Shift3.Qh
  N17: Shift2.A, S_Trig6.2Y
  N18: Shift2.B, S_Trig6.1Y
  N19: Shift2.C, S_Trig5.4Y
  N20: Shift2.D, S_Trig5.5Y
  N21: Shift3.E, S_Trig2.6Y
  N22: Shift3.F, S_Trig2.5Y
  N23: Shift3.G, S_Trig2.4Y
  N24: Shift3.H, S_Trig2.3Y
  N25: Shift3.Ser, Shift4.Qh
  N26: Shift3.A, S_Trig6.6Y
  N27: Shift3.B, S_Trig6.5Y
  N28: Shift3.C, S_Trig6.4Y
  N29: Shift3.D, S_Trig6.3Y
  N30: Shift4.E, S_Trig3.1Y
  N31: Shift4.F, S_Trig3.2Y
  N32: Shift4.G, S_Trig3.3Y
  N33: Shift4.H, S_Trig3.6Y
  N34: Shift4.A, S_Trig7.1Y
  N35: Shift4.B, S_Trig7.4Y
  N36: Shift4.C, S_Trig7.5Y
  N37: Shift4.D, S_Trig7.6Y
  N38: S_Trig1.1A, 1uF_cap_28.0, 10kOhm_R28.Pin_1
  N39: S_Trig1.2A, 1uF_cap_29.0, 10kOhm_R29.Pin_1
  N40: S_Trig1.3A, 1uF_cap_30.0, 10kOhm_R30.Pin_1
  N41: S_Trig1.4A, 1uF_cap_25.0, 10kOhm_R25.Pin_1
  N42: S_Trig1.5A, 1uF_cap_26.0, 10kOhm_R26.Pin_1
  N43: S_Trig1.6A, 1uF_cap_27.0, 10kOhm_R27.Pin_1
  N44: S_Trig2.1A, 1uF_cap_31.0, 10kOhm_R31.Pin_1
  N45: S_Trig2.2A, 1uF_cap_32.0, 10kOhm_R32.Pin_1
  N46: S_Trig2.3A, 1uF_cap_33.0, 10kOhm_R33.Pin_1
  N47: S_Trig2.4A, 1uF_cap_34.0, 10kOhm_R34.Pin_1
  N48: S_Trig2.5A, 1uF_cap_35.0, 10kOhm_R35.Pin_1
  N49: S_Trig2.6A, 1uF_cap_36.0, 10kOhm_R36.Pin_1
  N50: S_Trig4.1A, 1uF_cap_43.0, 10kOhm_R43.Pin_1
  N51: S_Trig4.2A, 1uF_cap_44.0, 10kOhm_R44.Pin_1
  N52: S_Trig4.3A, 1uF_cap_45.0, 10kOhm_R45.Pin_1
  N53: S_Trig4.4A, 1uF_cap_46.0, 10kOhm_R46.Pin_1
  N54: S_Trig4.5A, 1uF_cap_47.0, 10kOhm_R47.Pin_1
  N55: S_Trig4.6A, 1uF_cap_48.0, 10kOhm_R48.Pin_1
  N56: S_Trig5.1A, 1uF_cap_1.1, 10kOhm_R1.Pin_0
  N57: S_Trig5.2A, 1uF_cap_2.1, 10kOhm_R2.Pin_0
  N58: S_Trig5.3A, 1uF_cap_3.1, 10kOhm_R3.Pin_0
  N59: S_Trig5.4A, 1uF_cap_6.1, 10kOhm_R6.Pin_0
  N60: S_Trig5.5A, 1uF_cap_5.1, 10kOhm_R5.Pin_0
  N61: S_Trig5.6A, 1uF_cap_4.1, 10kOhm_R4.Pin_0
  N62: S_Trig6.1A, 1uF_cap_7.1, 10kOhm_R7.Pin_0
  N63: S_Trig6.2A, 1uF_cap_8.1, 10kOhm_R8.Pin_0
  N64: S_Trig6.3A, 1uF_cap_9.1, 10kOhm_R9.Pin_0
  N65: S_Trig6.4A, 1uF_cap_12.1, 10kOhm_R12.Pin_0
  N66: S_Trig6.5A, 1uF_cap_11.1, 10kOhm_R11.Pin_0
  N67: S_Trig6.6A, 1uF_cap_10.1, 10kOhm_R10.Pin_0
  N68: S_Trig7.1A, 1uF_cap_16.1, 10kOhm_R16.Pin_0
  N69: S_Trig7.2A, 1uF_cap_17.1, 10kOhm_R17.Pin_0
  N70: S_Trig7.3A, 1uF_cap_18.1, 10kOhm_R18.Pin_0
  N71: S_Trig7.4A, 1uF_cap_15.1, 10kOhm_R15.Pin_0
  N72: S_Trig7.5A, 1uF_cap_14.1, 10kOhm_R14.Pin_0
  N73: S_Trig7.6A, 1uF_cap_13.1, 10kOhm_R13.Pin_0
  N74: S_Trig8.1A, 1uF_cap_19.1, 10kOhm_R19.Pin_0
  N75: S_Trig8.2A, 1uF_cap_20.1, 10kOhm_R20.Pin_0
  N76: S_Trig8.3A, 1uF_cap_21.1, 10kOhm_R21.Pin_0
  N77: S_Trig8.4A, 1uF_cap_24.1, 10kOhm_R24.Pin_0
  N78: S_Trig8.5A, 1uF_cap_23.1, 10kOhm_R23.Pin_0
  N79: S_Trig8.6A, 1uF_cap_22.1, 10kOhm_R22.Pin_0
  N80: 1uF_cap_37.0, 10kOhm_R37.Pin_1, S_Trig3.1A
  N81: 1uF_cap_38.0, 10kOhm_R38.Pin_1, S_Trig3.2A
  N82: 1uF_cap_39.0, 10kOhm_R39.Pin_1, S_Trig3.3A
  N83: 1uF_cap_40.0, 10kOhm_R40.Pin_1, S_Trig3.6A
  N84: 1uF_cap_41.0, 10kOhm_R41.Pin_1, S_Trig3.4A
  N85: 1uF_cap_42.0, 10kOhm_R42.Pin_1, S_Trig3.5A
  N86: 10kOhm_R1.Pin_1, 100kOhm_R1.Pin_0
  N87: 10kOhm_R2.Pin_1, 100kOhm_R2.Pin_0
  N88: 10kOhm_R3.Pin_1, 100kOhm_R3.Pin_0
  N89: 10kOhm_R4.Pin_1, 100kOhm_R4.Pin_0
  N90: 10kOhm_R5.Pin_1, 100kOhm_R5.Pin_0
  N91: 10kOhm_R6.Pin_1, 100kOhm_R6.Pin_0
  N92: 10kOhm_R7.Pin_1, 100kOhm_R7.Pin_0
  N93: 10kOhm_R8.Pin_1, 100kOhm_R8.Pin_0
  N94: 10kOhm_R9.Pin_1, 100kOhm_R9.Pin_0
  N95: 10kOhm_R10.Pin_1, 100kOhm_R10.Pin_0
  N96: 10kOhm_R11.Pin_1, 100kOhm_R11.Pin_0
  N97: 10kOhm_R12.Pin_1, 100kOhm_R12.Pin_0
  N98: 10kOhm_R13.Pin_1, 100kOhm_R13.Pin_0
  N99: 10kOhm_R14.Pin_1, 100kOhm_R14.Pin_0
  N100: 10kOhm_R15.Pin_1, 100kOhm_R15.Pin_0
  N101: 10kOhm_R16.Pin_1, 100kOhm_R16.Pin_0
  N102: 10kOhm_R17.Pin_1, 100kOhm_R17.Pin_0
  N103: 10kOhm_R18.Pin_1, 100kOhm_R18.Pin_0
  N104: 10kOhm_R19.Pin_1, 100kOhm_R19.Pin_0
  N105: 10kOhm_R20.Pin_1, 100kOhm_R20.Pin_0
  N106: 10kOhm_R21.Pin_1, 100kOhm_R21.Pin_0
  N107: 10kOhm_R22.Pin_1, 100kOhm_R22.Pin_0
  N108: 10kOhm_R23.Pin_1, 100kOhm_R23.Pin_0
  N109: 10kOhm_R24.Pin_1, 100kOhm_R24.Pin_0
  N110: 10kOhm_R25.Pin_0, 100kOhm_R25.Pin_1
  N111: 10kOhm_R26.Pin_0, 100kOhm_R26.Pin_1
  N112: 10kOhm_R27.Pin_0, 100kOhm_R27.Pin_1
  N113: 10kOhm_R28.Pin_0, 100kOhm_R28.Pin_1
  N114: 10kOhm_R29.Pin_0, 100kOhm_R29.Pin_1
  N115: 10kOhm_R30.Pin_0, 100kOhm_R30.Pin_1
  N116: 10kOhm_R31.Pin_0, 100kOhm_R31.Pin_1
  N117: 10kOhm_R32.Pin_0, 100kOhm_R32.Pin_1
  N118: 10kOhm_R33.Pin_0, 100kOhm_R33.Pin_1
  N119: 10kOhm_R34.Pin_0, 100kOhm_R34.Pin_1
  N120: 10kOhm_R35.Pin_0, 100kOhm_R35.Pin_1
  N121: 10kOhm_R36.Pin_0, 100kOhm_R36.Pin_1
  N122: 10kOhm_R37.Pin_0, 100kOhm_R37.Pin_1
  N123: 10kOhm_R38.Pin_0, 100kOhm_R38.Pin_1
  N124: 10kOhm_R39.Pin_0, 100kOhm_R39.Pin_1
  N125: 10kOhm_R40.Pin_0, 100kOhm_R40.Pin_1
  N126: 10kOhm_R41.Pin_0, 100kOhm_R41.Pin_1
  N127: 10kOhm_R42.Pin_0, 100kOhm_R42.Pin_1
  N128: 10kOhm_R43.Pin_0, 100kOhm_R43.Pin_1
  N129: 10kOhm_R44.Pin_0, 100kOhm_R44.Pin_1
  N130: 10kOhm_R45.Pin_0, 100kOhm_R45.Pin_1
  N131: 10kOhm_R46.Pin_0, 100kOhm_R46.Pin_1
  N132: 10kOhm_R47.Pin_0, 100kOhm_R47.Pin_1
  N133: 100kOhm_R48.Pin_1, 10kOhm_R48.Pin_0

custom parts:
  SHIFT REGISTER: 8-bit SHIFT REGISTER, output latch
